# Fritzing sketch circuit (saved by Fritzing 0.9.3b)
circuit board: 8.46667cm x 5.64444cm
breadboards: 1

parts:
  Raspberry_Pi_1 = Raspberry Pi 3 [part_number=RPI-3-V1.2]
  IC1 = MCP3008 8-channel 10-bit ADC [part_number=MCP3008]
  Force_Sensor = Basic Force Sensing Resistor (FSR) [package=THT]
  R1 = Resistor [tolerance=±5% resistance=10k package="0805 [SMD]"]
  R2 = Resistor [tolerance=±5% resistance=560 package="0805 [SMD]"]
  LED1 = LED - 5mm [color="Red (633nm)" package="5 mm [THT]"]

nets:
  N1: Raspberry_Pi_1.3v3, IC1.no_name_yet#15, IC1.no_name_yet#16, Force_Sensor.pin_1
  N2: Raspberry_Pi_1.GND, IC1.no_name_yet#9, IC1.no_name_yet#14, R1.Pin_1, LED1.cathode
  N3: Raspberry_Pi_1.GIPO10, IC1.no_name_yet#11
  N4: Raspberry_Pi_1.GIPO9, IC1.no_name_yet#12
  N5: Raspberry_Pi_1.GIPO11, IC1.no_name_yet#13
  N6: Raspberry_Pi_1.GIPO5, R2.Pin_1
  N7: Raspberry_Pi_1.GIPO8, IC1.no_name_yet#10
  N8: IC1.no_name_yet#1, Force_Sensor.pin_0, R1.Pin_0
  N9: R2.Pin_0, LED1.anode
